# Fritzing sketch Fritzing sketch (saved by Fritzing 0.9.5d)
breadboards: 1

parts:
  WeMos_D1_Mini1 = WeMos D1 Mini
  WeMos_D1_Mini_Battery_Shield1 = WeMos D1 Mini Battery Shield
  WeMos_D1_Mini_Motor_Shield1 = WeMos D1 Mini Motor Shield
  M1 = DC Motor  # not connected
  M2 = DC Motor  # not connected
  BAT1 = Battery Holders [package=battery-aa-kit]  # not connected
  P1 = S1133 Si Photodiode [package="8mm Ceramic [THT]"]
  P2 = S1133 Si Photodiode [package="8mm Ceramic [THT]"]
  HC-SR04_Sensor_1 = HC-SR04 Ultrasonic Distance Sensor  # not connected
  LED1 = RGB LED (com. anode, rbg) [package="5 mm [THT]"]  # not connected

nets:
  3V3: WeMos_D1_Mini1.3V3, WeMos_D1_Mini_Battery_Shield1.3V3, P1.anode
  5V: WeMos_D1_Mini1.5V, WeMos_D1_Mini_Battery_Shield1.5V, WeMos_D1_Mini_Motor_Shield1.5V
  N1: WeMos_D1_Mini1.D1, WeMos_D1_Mini_Motor_Shield1.D1
  N2: WeMos_D1_Mini1.D2, WeMos_D1_Mini_Motor_Shield1.D2
  N3: WeMos_D1_Mini1.D8, P2.anode
  N4: WeMos_D1_Mini1.G, WeMos_D1_Mini_Battery_Shield1.G, WeMos_D1_Mini_Motor_Shield1.G, P1.cathode, P2.cathode
  N5: WeMos_D1_Mini1.RST, WeMos_D1_Mini_Motor_Shield1.RST
